// Logisim project TFArq.circ as structural Verilog: 15 circuits, main circuit CpuPipelined
module bancoRegistrador (
  input  [7:0] RegValue,
  input  RegWrite,
  input  [1:0] regDest,
  input  [1:0] RegA,
  input  [1:0] RegB,
  input  Reset,
  output [7:0] SaidaA,
  output [7:0] R0SAIDA,
  output [7:0] SaidaB
);

  wire clock_1_out, demultiplexer_1_out0, demultiplexer_1_out1, demultiplexer_1_out2, demultiplexer_1_out3;
  wire [7:0] r1_q, r2_q, r3_q;

  Demultiplexer #(.select(2)) demultiplexer_1 (
    .out0(demultiplexer_1_out0), .out1(demultiplexer_1_out1), .out2(demultiplexer_1_out2),
    .out3(demultiplexer_1_out3), .in(RegWrite), .sel(regDest));
  Register #(.trigger("falling")) r0 (
    .D(RegValue), .en(demultiplexer_1_out0), .clk(clock_1_out), .Q(R0SAIDA), .clr(Reset));
  Register #(.trigger("falling")) r1 (
    .D(RegValue), .en(demultiplexer_1_out1), .clk(clock_1_out), .Q(r1_q), .clr(Reset));
  Clock clock_1 (.out(clock_1_out));
  Register #(.trigger("falling")) r2 (
    .D(RegValue), .en(demultiplexer_1_out2), .clk(clock_1_out), .Q(r2_q), .clr(Reset));
  Register #(.trigger("falling")) r3 (
    .D(RegValue), .en(demultiplexer_1_out3), .clk(clock_1_out), .Q(r3_q), .clr(Reset));
  Multiplexer #(.select(2), .width(8)) multiplexer_1 (
    .in0(R0SAIDA), .in1(r1_q), .in2(r2_q), .in3(r3_q), .out(SaidaA), .sel(RegA));
  Multiplexer #(.select(2), .width(8)) multiplexer_2 (
    .in0(R0SAIDA), .in1(r1_q), .in2(r2_q), .in3(r3_q), .out(SaidaB), .sel(RegB));
endmodule

module Ula (
  input  [7:0] A,
  input  [7:0] B,
  input  [2:0] OpULA,
  output zero,
  output [7:0] saida
);

  wire [2:0] bit_extender_1_out;
  wire [7:0] adder_1_out, and_1_out, not_1_out, or_1_out, shifter_1_out, shifter_2_out, subtractor_1_out;

  assign not_1_out = ~B;  // NOT_Gate not_1, 8 bits wide
  Bit_Extender #(.out_width(3)) bit_extender_1 (.in(B), .out(bit_extender_1_out));
  Adder adder_1 (.a(A), .b(B), .out(adder_1_out));  // open: cin, cout
  Subtractor subtractor_1 (.a(A), .b(B), .out(subtractor_1_out));  // open: bin, bout
  assign and_1_out = A & B;  // AND_Gate and_1, 8 bits wide
  assign or_1_out = A | B;  // OR_Gate or_1, 8 bits wide
  Shifter shifter_1 (.in(A), .\dist (bit_extender_1_out), .out(shifter_1_out));
  Shifter shifter_2 (.in(A), .\dist (bit_extender_1_out), .out(shifter_2_out));
  Multiplexer #(.select(3), .width(8)) multiplexer_1 (
    .in0(adder_1_out), .in1(subtractor_1_out), .in2(and_1_out), .in3(or_1_out), .in4(not_1_out),
    .in5(shifter_1_out), .in6(shifter_2_out), .out(saida), .sel(OpULA));  // open: in7
  Comparator comparator_1 (.a({8{1'b0}}), .b(saida), .eq(zero));  // open: gt, lt

  // Notes on the sheet:
  //   XOR
  //   arruma
endmodule

module controle (
  input  [3:0] in_1,
  output [2:0] UlaControl,
  output [1:0] BranchType,
  output r0,
  output MemRead,
  output MemWrite,
  output [1:0] MuxWrite,
  output MuxUla,
  output RegWrite,
  output jump
);

  wire clock_1_out;
  wire [15:13] rom_1_data;

  Register #(.width(4)) ProvaIn (.D(in_1), .en(1'b1), .clk(clock_1_out));  // open: Q, clr
  Clock clock_1 (.out(clock_1_out));
  ROM #(.addrWidth(4), .dataWidth(16)) rom_1 (
    .addr(in_1),
    .data({rom_1_data, jump, RegWrite, MuxUla, MuxWrite, MemWrite, MemRead, r0, BranchType, UlaControl}));
  Register #(.width(16)) ProvaOut (
    .D({rom_1_data, jump, RegWrite, MuxUla, MuxWrite, MemWrite, MemRead, r0, BranchType, UlaControl}),
    .en(1'b1), .clk(clock_1_out));  // open: Q, clr

  // Notes on the sheet:
  //   contents of rom_1 (hex, n*v repeats v):
  //   800 c00 801 802 c02 803 c03 804 805 806 1029 1010 1a18 940 80
endmodule

module IFID (
  input  [7:0] InstIF,
  input  [7:0] PCIF,
  input  we,
  input  reset,
  output [7:0] instID,
  output [7:0] PCID
);

  wire clock_1_out;
  wire [7:0] multiplexer_1_out;

  Clock clock_1 (.out(clock_1_out));
  Multiplexer #(.width(8)) multiplexer_1 (.in0(InstIF), .in1(8'hf0), .out(multiplexer_1_out), .sel(reset));
  Register register_1 (.D(multiplexer_1_out), .en(we), .clk(clock_1_out), .Q(instID));  // open: clr
  Register register_2 (.D(PCIF), .en(we), .clk(clock_1_out), .Q(PCID), .clr(reset));
endmodule

module IDEX (
  input  [7:0] pcID,
  input  [7:0] Rs1AID,
  input  [7:0] Rs2BID,
  input  [7:0] R0ID,
  input  [7:0] ImmID,
  input  [2:0] UlaCtrlID,
  input  [1:0] BranchTID,
  input  r0ctrlID,
  input  MemReadID,
  input  MemWriteID,
  input  [1:0] MuxWriteID,
  input  MuxUlaID,
  input  RegWriteID,
  input  jumpID,
  input  [3:0] opcode,
  input  [1:0] regDestID,
  input  we,
  input  reset,
  output [7:0] pcEX,
  output [7:0] Rs1AEX,
  output [7:0] Rs2BEX,
  output [7:0] R0EX,
  output [7:0] immEX,
  output [2:0] UlaCtrlEX,
  output [1:0] BranchTEX,
  output r0ctrlEX,
  output MemReadEX,
  output MemWriteEX,
  output [1:0] MuxWriteEX,
  output MuxUlaEX,
  output RegWriteEX,
  output jumpEX,
  output [3:0] opcodeEX,
  output [1:0] regDestEX
);

  wire clock_1_out, or_1_out;
  wire [3:0] multiplexer_1_out;

  Clock clock_1 (.out(clock_1_out));
  Register register_1 (.D(pcID), .en(we), .clk(clock_1_out), .Q(pcEX), .clr(reset));
  Register register_2 (.D(Rs1AID), .en(we), .clk(clock_1_out), .Q(Rs1AEX), .clr(reset));
  Register register_3 (.D(Rs2BID), .en(we), .clk(clock_1_out), .Q(Rs2BEX), .clr(reset));
  Register register_4 (.D(R0ID), .en(we), .clk(clock_1_out), .Q(R0EX), .clr(reset));
  Register register_5 (.D(ImmID), .en(we), .clk(clock_1_out), .Q(immEX), .clr(reset));
  Register #(.width(3)) register_6 (.D(UlaCtrlID), .en(we), .clk(clock_1_out), .Q(UlaCtrlEX), .clr(reset));
  Register #(.width(2)) register_7 (.D(BranchTID), .en(we), .clk(clock_1_out), .Q(BranchTEX), .clr(reset));
  Register #(.width(1)) register_8 (.D(r0ctrlID), .en(we), .clk(clock_1_out), .Q(r0ctrlEX), .clr(reset));
  Register #(.width(1)) register_9 (.D(MemReadID), .en(we), .clk(clock_1_out), .Q(MemReadEX), .clr(reset));
  Register #(.width(1)) register_10 (.D(MemWriteID), .en(we), .clk(clock_1_out), .Q(MemWriteEX), .clr(reset));
  Register #(.width(2)) register_11 (.D(MuxWriteID), .en(we), .clk(clock_1_out), .Q(MuxWriteEX), .clr(reset));
  Register #(.width(1)) register_12 (.D(MuxUlaID), .en(we), .clk(clock_1_out), .Q(MuxUlaEX), .clr(reset));
  Register #(.width(1)) register_13 (.D(RegWriteID), .en(we), .clk(clock_1_out), .Q(RegWriteEX), .clr(reset));
  Register #(.width(1)) register_14 (.D(jumpID), .en(we), .clk(clock_1_out), .Q(jumpEX), .clr(reset));
  Register #(.width(2)) register_15 (.D(regDestID), .en(we), .clk(clock_1_out), .Q(regDestEX), .clr(reset));
  Multiplexer #(.width(4)) multiplexer_1 (.in0(opcode), .in1(4'b1111), .out(multiplexer_1_out), .sel(reset));
  or or_1 (or_1_out, we, reset);
  Register #(.width(4)) register_16 (
    .D(multiplexer_1_out), .en(or_1_out), .clk(clock_1_out), .Q(opcodeEX));  // open: clr
endmodule

module EXMEM (
  input  [7:0] pcEX,
  input  [7:0] NewPCEX,
  input  [7:0] ulaEX,
  input  [7:0] Rs1EX,
  input  jumpEX,
  input  memReadEX,
  input  memWriteEX,
  input  [1:0] muxWriteEX,
  input  regWriteEX,
  input  [1:0] regDestEX,
  input  [3:0] opcode,
  input  [7:0] rs2,
  input  we,
  input  reset,
  output [7:0] pcMEM,
  output [7:0] NewPcMem,
  output [7:0] ulaMEM,
  output [7:0] rs1MEM,
  output jumpMEM,
  output memReadMEM,
  output memWriteMEM,
  output [1:0] muxWriteMEM,
  output regWriteMEM,
  output [1:0] regDestMEM,
  output [3:0] opcodeMEM,
  output [7:0] rs2MEM
);

  wire clock_1_out;

  Clock clock_1 (.out(clock_1_out));
  Register register_1 (.D(pcEX), .en(we), .clk(clock_1_out), .Q(pcMEM), .clr(reset));
  Register register_2 (.D(NewPCEX), .en(we), .clk(clock_1_out), .Q(NewPcMem), .clr(reset));
  Register register_3 (.D(ulaEX), .en(we), .clk(clock_1_out), .Q(ulaMEM), .clr(reset));
  Register register_4 (.D(Rs1EX), .en(we), .clk(clock_1_out), .Q(rs1MEM), .clr(reset));
  Register #(.width(1)) register_5 (.D(jumpEX), .en(we), .clk(clock_1_out), .Q(jumpMEM), .clr(reset));
  Register #(.width(1)) register_6 (.D(memReadEX), .en(we), .clk(clock_1_out), .Q(memReadMEM), .clr(reset));
  Register #(.width(1)) register_7 (.D(memWriteEX), .en(we), .clk(clock_1_out), .Q(memWriteMEM), .clr(reset));
  Register #(.width(2)) register_8 (.D(muxWriteEX), .en(we), .clk(clock_1_out), .Q(muxWriteMEM), .clr(reset));
  Register #(.width(1)) register_9 (.D(regWriteEX), .en(we), .clk(clock_1_out), .Q(regWriteMEM), .clr(reset));
  Register #(.width(2)) register_10 (.D(regDestEX), .en(we), .clk(clock_1_out), .Q(regDestMEM), .clr(reset));
  Register #(.width(4)) register_11 (.D(opcode), .en(we), .clk(clock_1_out), .Q(opcodeMEM), .clr(reset));
  Register register_12 (.D(rs2), .en(we), .clk(clock_1_out), .Q(rs2MEM), .clr(reset));
endmodule

module MEMWB (
  input  [7:0] pcMEM,
  input  [7:0] NewPCMEM,
  input  [7:0] memToRegMEM,
  input  [7:0] ulaToRegMEM,
  input  jumpMEM,
  input  [1:0] muxWriteEX,
  input  regWriteEX,
  input  [1:0] regDestEX,
  input  [3:0] opcode,
  input  we,
  input  reset,
  output [7:0] pcWB,
  output [7:0] NewPCWB,
  output [7:0] memToRegWB,
  output [7:0] ulaToRegWB,
  output jumpWB,
  output [1:0] muxWriteMEM,
  output regWriteMEM,
  output [1:0] regDestmem,
  output [3:0] opcodeWB
);

  wire clock_1_out;

  Clock clock_1 (.out(clock_1_out));
  Register register_1 (.D(pcMEM), .en(we), .clk(clock_1_out), .Q(pcWB), .clr(reset));
  Register register_2 (.D(NewPCMEM), .en(we), .clk(clock_1_out), .Q(NewPCWB), .clr(reset));
  Register register_3 (.D(memToRegMEM), .en(we), .clk(clock_1_out), .Q(memToRegWB), .clr(reset));
  Register register_4 (.D(ulaToRegMEM), .en(we), .clk(clock_1_out), .Q(ulaToRegWB), .clr(reset));
  Register #(.width(1)) register_5 (.D(jumpMEM), .en(we), .clk(clock_1_out), .Q(jumpWB), .clr(reset));
  Register #(.width(2)) register_6 (.D(muxWriteEX), .en(we), .clk(clock_1_out), .Q(muxWriteMEM), .clr(reset));
  Register #(.width(1)) register_7 (.D(regWriteEX), .en(we), .clk(clock_1_out), .Q(regWriteMEM), .clr(reset));
  Register #(.width(2)) register_8 (.D(regDestEX), .en(we), .clk(clock_1_out), .Q(regDestmem), .clr(reset));
  Register #(.width(4)) register_9 (.D(opcode), .en(we), .clk(clock_1_out), .Q(opcodeWB), .clr(reset));
endmodule

module branchModule (
  input  [7:0] PC,
  input  [7:0] rs2,
  input  zero,
  input  [1:0] branchType,
  output jump,
  output [7:0] NewPC
);

  wire comparator_1_eq;
  wire [7:0] multiplexer_1_out;

  Multiplexer #(.width(8)) multiplexer_1 (.in0(PC), .in1(rs2), .out(multiplexer_1_out), .sel(zero));
  Multiplexer #(.select(2), .width(8)) multiplexer_2 (
    .in0(PC), .in1(multiplexer_1_out), .in2(rs2), .in3(rs2), .out(NewPC), .sel(branchType));
  Comparator comparator_1 (.a(PC), .b(NewPC), .eq(comparator_1_eq));  // open: gt, lt
  not not_1 (jump, comparator_1_eq);
endmodule

module CpuPipelined (
);

  wire branchmodule_1_jump, cache_1_miss, cachetomemory_1_memread, cachetomemory_1_memwrite, clk, clkDiv2,
       clock_2_out, clock_3_out, controle_1_jump, controle_1_memread, controle_1_memwrite, controle_1_muxula,
       controle_1_r0, controle_1_regwrite, exmem_1_jumpmem, exmem_1_memreadmem, exmem_1_memwritemem,
       exmem_1_regwritemem, fimWB, hzExMemRS2, hzExWbRS1, hzExWbRS2, hzRxMemRS1, idex_1_memreadex,
       idex_1_memwriteex, idex_1_muxulaex, idex_1_r0ctrlex, idex_1_regwriteex, limpaPipe, memwb_1_jumpwb,
       memwb_1_regwritemem, multiplexer_10_out, multiplexer_11_out, not_1_out, not_2_out, reset, stall,
       ula_1_zero;
  wire [1:0] controle_1_branchtype, controle_1_muxwrite, exmem_1_muxwritemem, exmem_1_regdestmem,
       idex_1_branchtex, idex_1_muxwriteex, idex_1_regdestex, memwb_1_muxwritemem, memwb_1_regdestmem,
       selectedReg1, selectedReg2;
  wire [2:0] controle_1_ulacontrol, idex_1_ulactrlex;
  wire [3:0] cache_1_tagr0, cache_1_tagr1, cache_1_tagr2, cache_1_tagr3, contador_1_dozeaquinze,
       contador_1_oitoaonze, contador_1_quatroasete, contador_1_zeroatres, counter_1_q, counter_1_q_2,
       counter_1_q_3, counter_1_q_4, exmem_1_opcodemem, idex_1_opcodeex, memwb_1_opcodewb;
  wire [7:0] bancoregistrador_1_r0saida, bancoregistrador_1_saidaa, bancoregistrador_1_saidab,
       bit_extender_1_out, branchmodule_1_newpc, cache_1_data_out, cachetomemory_1_memaddress,
       cachetomemory_1_memvalue, exmem_1_newpcmem, exmem_1_pcmem, exmem_1_rs1mem, exmem_1_rs2mem,
       exmem_1_ulamem, hazardunity_1_hazardvalue, idex_1_immex, idex_1_pcex, idex_1_r0ex, idex_1_rs1aex,
       idex_1_rs2bex, ifid_1_pcid, memwb_1_memtoregwb, memwb_1_newpcwb, memwb_1_pcwb, memwb_1_ulatoregwb,
       mPrincipal, multiplexer_1_out, multiplexer_2_out, multiplexer_3_out, multiplexer_4_out,
       multiplexer_5_out, multiplexer_6_out, multiplexer_7_out, multiplexer_8_out, multiplexer_9_out,
       pc_1_saidapc, pc_1_saidapc2, rom_1_data, ula_1_saida;
  wire [7:4] ifid_1_instid;

  Clock clock_1 (.out(clk));
  Button button_1 (.out(reset));
  PC pc_1 (
    .Jump(memwb_1_jumpwb), .NewPC(memwb_1_newpcwb), .Stall(stall), .Clock(clk), .Reset(reset),
    .LimpaPipe(limpaPipe), .SaidaPC(pc_1_saidapc), .SaidaPC2(pc_1_saidapc2), .ClockDiv2(clkDiv2));
  ROM rom_1 (.addr(pc_1_saidapc2), .data(rom_1_data));
  Contador contador_1 (
    .botao(rom_1_data), .Clock(clk), .ZeroAtres(contador_1_zeroatres), .QuatroASete(contador_1_quatroasete),
    .OitoAOnze(contador_1_oitoaonze), .DozeAQuinze(contador_1_dozeaquinze));
  Hex_Digit_Display hex_digit_display_1 (.value(contador_1_dozeaquinze));  // open: dp
  not not_1 (not_1_out, stall);
  Hex_Digit_Display hex_digit_display_2 (.value(contador_1_quatroasete));  // open: dp
  Hex_Digit_Display hex_digit_display_3 (.value(contador_1_oitoaonze));  // open: dp
  IFID ifid_1 (
    .InstIF(rom_1_data), .PCIF(pc_1_saidapc), .we(not_1_out), .reset(limpaPipe),
    .instID({ifid_1_instid, selectedReg2, selectedReg1}), .PCID(ifid_1_pcid));
  Hex_Digit_Display hex_digit_display_4 (.value(contador_1_zeroatres));  // open: dp
  controle controle_1 (
    .in_1(ifid_1_instid), .UlaControl(controle_1_ulacontrol), .BranchType(controle_1_branchtype),
    .r0(controle_1_r0), .MemRead(controle_1_memread), .MemWrite(controle_1_memwrite),
    .MuxWrite(controle_1_muxwrite), .MuxUla(controle_1_muxula), .RegWrite(controle_1_regwrite),
    .jump(controle_1_jump));
  hazardUnity hazardunity_1 (
    .opcodeEXMEM(exmem_1_opcodemem), .ulaToHmodule(exmem_1_ulamem), .memToHmodule(cache_1_data_out),
    .opcoWB(memwb_1_opcodewb), .selectedReg1(selectedReg1), .opcodeIDEX(idex_1_opcodeex), .clk(clk),
    .selectedReg2(selectedReg2), .reset(reset), .hzRS1(hzRxMemRS1), .hzRS2(hzExMemRS2),
    .hzLongoRS1(hzExWbRS1), .hazardValue(hazardunity_1_hazardvalue), .hzLongoRs2(hzExWbRS2));
  assign bit_extender_1_out = {{6{1'b0}}, selectedReg2};  // Bit_Extender bit_extender_1
  bancoRegistrador bancoregistrador_1 (
    .RegValue(multiplexer_7_out), .RegWrite(memwb_1_regwritemem), .regDest(memwb_1_regdestmem),
    .RegA(selectedReg1), .RegB(selectedReg2), .Reset(reset), .SaidaA(bancoregistrador_1_saidaa),
    .R0SAIDA(bancoregistrador_1_r0saida), .SaidaB(bancoregistrador_1_saidab));
  IDEX idex_1 (
    .BranchTID(controle_1_branchtype), .r0ctrlID(controle_1_r0), .MemReadID(controle_1_memread),
    .MemWriteID(controle_1_memwrite), .MuxWriteID(controle_1_muxwrite), .MuxUlaID(controle_1_muxula),
    .RegWriteID(controle_1_regwrite), .jumpID(controle_1_jump), .opcode(ifid_1_instid),
    .regDestID(selectedReg1), .Rs1AID(bancoregistrador_1_saidaa), .Rs2BID(bancoregistrador_1_saidab),
    .R0ID(bancoregistrador_1_r0saida), .ImmID(bit_extender_1_out), .pcID(ifid_1_pcid),
    .UlaCtrlID(controle_1_ulacontrol), .we(not_1_out), .reset(limpaPipe), .RegWriteEX(idex_1_regwriteex),
    .regDestEX(idex_1_regdestex), .BranchTEX(idex_1_branchtex), .r0ctrlEX(idex_1_r0ctrlex),
    .MemReadEX(idex_1_memreadex), .MemWriteEX(idex_1_memwriteex), .MuxWriteEX(idex_1_muxwriteex),
    .MuxUlaEX(idex_1_muxulaex), .Rs1AEX(idex_1_rs1aex), .Rs2BEX(idex_1_rs2bex), .R0EX(idex_1_r0ex),
    .immEX(idex_1_immex), .pcEX(idex_1_pcex), .UlaCtrlEX(idex_1_ulactrlex), .opcodeEX(idex_1_opcodeex));  // open: jumpEX
  Multiplexer #(.width(8)) multiplexer_1 (
    .in0(idex_1_rs2bex), .in1(multiplexer_7_out), .out(multiplexer_1_out), .sel(hzExWbRS2));
  Multiplexer #(.width(8)) multiplexer_2 (
    .in0(multiplexer_1_out), .in1(hazardunity_1_hazardvalue), .out(multiplexer_2_out), .sel(hzExMemRS2));
  Multiplexer #(.width(8)) multiplexer_3 (
    .in0(multiplexer_2_out), .in1(idex_1_r0ex), .out(multiplexer_3_out), .sel(idex_1_r0ctrlex));
  Multiplexer #(.width(8)) multiplexer_4 (
    .in0(idex_1_rs1aex), .in1(multiplexer_7_out), .out(multiplexer_4_out), .sel(hzExWbRS1));
  Multiplexer #(.width(8)) multiplexer_5 (
    .in0(multiplexer_3_out), .in1(idex_1_immex), .out(multiplexer_5_out), .sel(idex_1_muxulaex));
  Multiplexer #(.width(8)) multiplexer_6 (
    .in0(multiplexer_4_out), .in1(hazardunity_1_hazardvalue), .out(multiplexer_6_out), .sel(hzRxMemRS1));
  Multiplexer #(.select(2), .width(8)) multiplexer_7 (
    .in0(memwb_1_ulatoregwb), .in1(memwb_1_memtoregwb), .in2(memwb_1_pcwb), .out(multiplexer_7_out),
    .sel(memwb_1_muxwritemem));  // open: in3
  Ula ula_1 (
    .A(multiplexer_6_out), .B(multiplexer_5_out), .OpULA(idex_1_ulactrlex), .zero(ula_1_zero),
    .saida(ula_1_saida));
  Hex_Digit_Display hex_digit_display_5 (.value(counter_1_q_4));  // open: dp
  Hex_Digit_Display hex_digit_display_6 (.value(counter_1_q_3));  // open: dp
  Hex_Digit_Display hex_digit_display_7 (.value(counter_1_q_2));  // open: dp
  branchModule branchmodule_1 (
    .PC(idex_1_pcex), .zero(ula_1_zero), .branchType(idex_1_branchtex), .rs2(multiplexer_2_out),
    .NewPC(branchmodule_1_newpc), .jump(branchmodule_1_jump));
  Hex_Digit_Display hex_digit_display_8 (.value(counter_1_q));  // open: dp
  EXMEM exmem_1 (
    .pcEX(idex_1_pcex), .NewPCEX(branchmodule_1_newpc), .ulaEX(ula_1_saida), .Rs1EX(multiplexer_6_out),
    .jumpEX(branchmodule_1_jump), .memReadEX(idex_1_memreadex), .memWriteEX(idex_1_memwriteex),
    .muxWriteEX(idex_1_muxwriteex), .regDestEX(idex_1_regdestex), .opcode(idex_1_opcodeex),
    .rs2(multiplexer_2_out), .regWriteEX(idex_1_regwriteex), .we(not_1_out), .reset(limpaPipe),
    .pcMEM(exmem_1_pcmem), .NewPcMem(exmem_1_newpcmem), .ulaMEM(exmem_1_ulamem), .rs1MEM(exmem_1_rs1mem),
    .jumpMEM(exmem_1_jumpmem), .memReadMEM(exmem_1_memreadmem), .memWriteMEM(exmem_1_memwritemem),
    .muxWriteMEM(exmem_1_muxwritemem), .regDestMEM(exmem_1_regdestmem), .opcodeMEM(exmem_1_opcodemem),
    .rs2MEM(exmem_1_rs2mem), .regWriteMEM(exmem_1_regwritemem));
  Counter #(.max('hffff), .width(16)) counter_1 (
    .Q({counter_1_q_4, counter_1_q_3, counter_1_q_2, counter_1_q}), .clk(cache_1_miss), .clr(1'b0));  // open: load, D, count, carry, up
  Multiplexer #(.width(8)) multiplexer_8 (
    .in0(exmem_1_rs2mem), .in1(cachetomemory_1_memaddress), .out(multiplexer_8_out), .sel(stall));
  Multiplexer #(.width(8)) multiplexer_9 (.in0(exmem_1_rs1mem), .in1(mPrincipal), .out(multiplexer_9_out), .sel(stall));
  Multiplexer multiplexer_10 (.in0(exmem_1_memreadmem), .in1(not_2_out), .out(multiplexer_10_out));  // open: sel
  Clock clock_2 (.out(clock_2_out));
  cache cache_1 (
    .memRead(multiplexer_10_out), .address(multiplexer_8_out), .data_in(multiplexer_9_out),
    .memWrite(multiplexer_11_out), .clk(clock_3_out), .R(reset), .data_out(cache_1_data_out),
    .miss(cache_1_miss), .tagR3(cache_1_tagr3), .tagR2(cache_1_tagr2), .tagR1(cache_1_tagr1),
    .tagR0(cache_1_tagr0));
  Multiplexer multiplexer_11 (.in0(exmem_1_memwritemem), .in1(fimWB), .out(multiplexer_11_out));  // open: sel
  not not_2 (not_2_out, fimWB);
  Clock clock_3 (.out(clock_3_out));
  cacheToMemory cachetomemory_1 (
    .address(exmem_1_rs2mem), .miss(cache_1_miss), .in_3(clock_2_out), .reset(reset), .tagR0(cache_1_tagr0),
    .tagR1(cache_1_tagr1), .tagR2(cache_1_tagr2), .tagR3(cache_1_tagr3), .clkMem(clkDiv2),
    .cacheIn(cache_1_data_out), .memAddress(cachetomemory_1_memaddress), .memWrite(cachetomemory_1_memwrite),
    .memRead(cachetomemory_1_memread), .memValue(cachetomemory_1_memvalue), .stall(stall), .fimWb(fimWB));
  MEMWB memwb_1 (
    .pcMEM(exmem_1_pcmem), .NewPCMEM(exmem_1_newpcmem), .memToRegMEM(cache_1_data_out),
    .ulaToRegMEM(exmem_1_ulamem), .regDestEX(exmem_1_regdestmem), .opcode(exmem_1_opcodemem),
    .jumpMEM(exmem_1_jumpmem), .muxWriteEX(exmem_1_muxwritemem), .regWriteEX(exmem_1_regwritemem),
    .we(not_1_out), .reset(limpaPipe), .pcWB(memwb_1_pcwb), .NewPCWB(memwb_1_newpcwb),
    .memToRegWB(memwb_1_memtoregwb), .ulaToRegWB(memwb_1_ulatoregwb), .regDestmem(memwb_1_regdestmem),
    .opcodeWB(memwb_1_opcodewb), .jumpWB(memwb_1_jumpwb), .muxWriteMEM(memwb_1_muxwritemem),
    .regWriteMEM(memwb_1_regwritemem));
  RAM #(.trigger("falling")) ram_1 (
    .addr(cachetomemory_1_memaddress), .we(cachetomemory_1_memwrite), .oe(cachetomemory_1_memread),
    .clk(clkDiv2), .din(cachetomemory_1_memvalue), .dout(mPrincipal));

  // Notes on the sheet:
  //   contents of rom_1 (hex, n*v repeats v):
  //   1e 1e 6*8 b b b 7*f0 a1 e5 9 5*f0 bc 9*f0 2f f0 f0 f0 ed f0 f0 f0 4*1b 4*f0 ed 1b 1b f0 f0 f0 ed ff
  //   ff f0 f0 f0 ed 79*ff
  //   imm
endmodule

module hazardUnity (
  input  [7:0] ulaToHmodule,
  input  [7:0] memToHmodule,
  input  [3:0] opcodeEXMEM,
  input  [3:0] opcoWB,
  input  [3:0] opcodeIDEX,
  input  [1:0] selectedReg1,
  input  clk,
  input  reset,
  input  [1:0] selectedReg2,
  output [7:0] hazardValue,
  output hzRS1,
  output hzRS2,
  output hzLongoRS1,
  output hzLongoRs2
);

  wire and_1_out, and_2_out, and_3_out, and_7_out, comparator_1_eq, comparator_2_eq, comparator_3_eq,
       comparator_4_eq, undriven, undriven_2, undriven_3, undriven_4, undriven_5;
  wire [1:0] register_1_q, register_2_q, register_3_q, register_4_q, register_5_q, register_6_q;

  Register #(.width(2)) register_1 (.D(selectedReg1), .en(1'b1), .clk(clk), .Q(register_1_q), .clr(reset));
  Register #(.width(2)) register_2 (.D(selectedReg2), .en(1'b1), .clk(clk), .Q(register_2_q), .clr(reset));
  ROM #(.addrWidth(4), .dataWidth(1)) rom_1 (.addr(opcodeIDEX));  // open: data
  ROM #(.addrWidth(4), .dataWidth(1)) rom_2 (.addr(opcodeIDEX));  // open: data
  Comparator #(.width(2)) comparator_1 (.a(register_4_q), .b(register_1_q), .eq(comparator_1_eq));  // open: gt, lt
  Comparator #(.width(2)) comparator_2 (.a(register_4_q), .b(register_2_q), .eq(comparator_2_eq));  // open: gt, lt
  Comparator #(.width(2)) comparator_3 (.a(register_1_q), .b(register_5_q), .eq(comparator_3_eq));  // open: gt, lt
  Register #(.width(2)) register_3 (.D(register_2_q), .en(1'b1), .clk(clk), .Q(register_3_q), .clr(reset));
  Register #(.width(2)) register_4 (.D(register_1_q), .en(1'b1), .clk(clk), .Q(register_4_q), .clr(reset));
  and and_1 (and_1_out, comparator_1_eq, undriven_2);
  and and_2 (and_2_out, undriven, comparator_2_eq);
  and and_3 (and_3_out, undriven_2, comparator_3_eq);
  Comparator #(.width(2)) comparator_4 (.a(register_6_q), .b(register_3_q), .eq(comparator_4_eq));  // open: gt, lt
  ROM #(.addrWidth(4), .dataWidth(1)) rom_3 (.addr(opcodeEXMEM));  // open: data
  and and_4 (hzRS1, and_1_out, undriven_4);
  and and_5 (hzRS2, and_2_out, undriven_4);
  and and_6 (hzLongoRS1, and_3_out, undriven_5);
  Multiplexer #(.width(8)) multiplexer_1 (.in0(ulaToHmodule), .in1(memToHmodule), .out(hazardValue), .sel(and_7_out));
  ROM #(.addrWidth(4), .dataWidth(1)) rom_4 (.addr(opcodeEXMEM));  // open: data
  and and_7 (and_7_out, undriven_3, undriven_2);
  Register #(.width(2)) register_5 (.D(register_4_q), .en(1'b1), .clk(clk), .Q(register_5_q), .clr(reset));
  and and_8 (hzLongoRs2, undriven_5, comparator_4_eq);
  ROM #(.addrWidth(4), .dataWidth(1)) rom_5 (.addr(opcoWB));  // open: data
  Register #(.width(2)) register_6 (.D(register_5_q), .en(1'b1), .clk(clk), .Q(register_6_q), .clr(reset));

  // Notes on the sheet:
  //   ID
  //   contents of rom_1 (hex, n*v repeats v):
  //   13*1
  //   contents of rom_2 (hex, n*v repeats v):
  //   1 0 1 1 0 1 0 4*1 0 1 1
  //   EX
  //   contents of rom_3 (hex, n*v repeats v):
  //   13*0 1
  //   contents of rom_4 (hex, n*v repeats v):
  //   13*1
  //   MEM
  //   contents of rom_5 (hex, n*v repeats v):
  //   10*1 0 1 1
  //   WB
endmodule

module cache (
  input  memRead,
  input  [7:0] address,
  input  [7:0] data_in,
  input  memWrite,
  input  clk,
  input  R,
  output miss,
  output [3:0] tagR3,
  output [3:0] tagR2,
  output [3:0] tagR1,
  output [3:0] tagR0,
  output [7:0] data_out
);

  wire cacheentry_1_miss, cacheentry_2_miss, cacheentry_3_miss, cacheentry_4_miss, demultiplexer_1_out0,
       demultiplexer_1_out1, demultiplexer_1_out2, demultiplexer_1_out3, demultiplexer_2_out0,
       demultiplexer_2_out1, demultiplexer_2_out2, demultiplexer_2_out3;
  wire [7:0] cacheentry_1_data_out, cacheentry_2_data_out, cacheentry_3_data_out, cacheentry_4_data_out;

  Multiplexer #(.select(2)) multiplexer_1 (
    .in0(cacheentry_4_miss), .in1(cacheentry_3_miss), .in2(cacheentry_2_miss), .in3(cacheentry_1_miss),
    .out(miss), .sel(address[3:2]));
  Demultiplexer #(.select(2)) demultiplexer_1 (
    .out0(demultiplexer_1_out0), .out1(demultiplexer_1_out1), .out2(demultiplexer_1_out2),
    .out3(demultiplexer_1_out3), .in(memRead), .sel(address[3:2]));
  Demultiplexer #(.select(2)) demultiplexer_2 (
    .out0(demultiplexer_2_out0), .out1(demultiplexer_2_out1), .out2(demultiplexer_2_out2),
    .out3(demultiplexer_2_out3), .in(memWrite), .sel(address[3:2]));
  cacheEntry cacheentry_1 (
    .memWrite(demultiplexer_2_out3), .tag(address[7:4]), .data_in(data_in), .byte_offset(address[1:0]),
    .clk(clk), .R(R), .memRead(demultiplexer_1_out3), .miss(cacheentry_1_miss), .out_9(tagR3),
    .data_out(cacheentry_1_data_out));
  cacheEntry cacheentry_2 (
    .memWrite(demultiplexer_2_out2), .tag(address[7:4]), .data_in(data_in), .byte_offset(address[1:0]),
    .clk(clk), .R(R), .memRead(demultiplexer_1_out2), .miss(cacheentry_2_miss), .out_9(tagR2),
    .data_out(cacheentry_2_data_out));
  cacheEntry cacheentry_3 (
    .memWrite(demultiplexer_2_out1), .tag(address[7:4]), .data_in(data_in), .byte_offset(address[1:0]),
    .clk(clk), .R(R), .memRead(demultiplexer_1_out1), .miss(cacheentry_3_miss), .out_9(tagR1),
    .data_out(cacheentry_3_data_out));
  cacheEntry cacheentry_4 (
    .memWrite(demultiplexer_2_out0), .tag(address[7:4]), .data_in(data_in), .byte_offset(address[1:0]),
    .clk(clk), .R(R), .memRead(demultiplexer_1_out0), .miss(cacheentry_4_miss), .out_9(tagR0),
    .data_out(cacheentry_4_data_out));
  Multiplexer #(.select(2), .width(8)) multiplexer_2 (
    .in0(cacheentry_4_data_out), .in1(cacheentry_3_data_out), .in2(cacheentry_2_data_out),
    .in3(cacheentry_1_data_out), .out(data_out), .sel(address[3:2]));

  // Other names for the same wires on the sheet: index[1:0] = address[3:2]

  // Notes on the sheet:
  //   offset
  //   index
  //   tag
endmodule

module cacheEntry (
  input  memRead,
  input  [3:0] tag,
  input  clk,
  input  memWrite,
  input  [1:0] byte_offset,
  input  [7:0] data_in,
  input  R,
  output miss,
  output [3:0] out_9,
  output [7:0] data_out
);

  wire comparator_1_eq, demultiplexer_1_out0, demultiplexer_1_out1, demultiplexer_1_out2,
       demultiplexer_1_out3, not_1_out, or_1_out, or_2_out;
  wire [7:0] register_1_q, register_2_q, register_3_q, register_4_q;

  or or_1 (or_1_out, memWrite, miss);
  Demultiplexer #(.select(2)) demultiplexer_1 (
    .out0(demultiplexer_1_out0), .out1(demultiplexer_1_out1), .out2(demultiplexer_1_out2),
    .out3(demultiplexer_1_out3), .in(or_1_out), .sel(byte_offset));
  Register #(.width(4)) tagR (.D(tag), .en(miss), .clk(clk), .Q(out_9), .clr(R));
  Register register_1 (.D(data_in), .en(demultiplexer_1_out0), .clk(clk), .Q(register_1_q), .clr(R));
  Register register_2 (.D(data_in), .en(demultiplexer_1_out1), .clk(clk), .Q(register_2_q), .clr(R));
  Register register_3 (.D(data_in), .en(demultiplexer_1_out2), .clk(clk), .Q(register_3_q), .clr(R));
  Register register_4 (.D(data_in), .en(demultiplexer_1_out3), .clk(clk), .Q(register_4_q), .clr(R));
  Comparator #(.width(4)) comparator_1 (.a(out_9), .b(tag), .eq(comparator_1_eq));  // open: gt, lt
  Multiplexer #(.select(2), .width(8)) multiplexer_1 (
    .in0(register_1_q), .in1(register_2_q), .in2(register_3_q), .in3(register_4_q), .out(data_out),
    .sel(byte_offset));
  or or_2 (or_2_out, memWrite, memRead);
  not not_1 (not_1_out, comparator_1_eq);
  and and_1 (miss, or_2_out, not_1_out);
endmodule

module cacheToMemory (
  input  [7:0] address,
  input  miss,
  input  in_3,
  input  reset,
  input  [3:0] tagR0,
  input  [3:0] tagR1,
  input  [3:0] tagR2,
  input  [3:0] tagR3,
  input  clkMem,
  input  [7:0] cacheIn,
  output [7:0] memAddress,
  output fimWb,
  output memWrite,
  output memRead,
  output [7:0] memValue,
  output stall
);

  wire and_2_out, not_1_out, not_2_out, not_3_out, not_4_out, novoBlocoPronto, or_1_out;
  wire [1:0] register_3_q, subtractor_1_out;
  wire [2:0] adder_1_out, adder_2_out, register_2_q;
  wire [2:2] register_3_q_2;
  wire [3:0] multiplexer_2_out;
  wire [3:2] multiplexer_1_out;

  Multiplexer #(.select(2), .width(2)) multiplexer_1 (
    .in0(2'b00), .in1(2'b01), .in2(2'b10), .in3(2'b11), .out(multiplexer_1_out), .sel(address[3:2]));
  Register #(.trigger("falling"), .width(1)) register_1 (.D(1'b1), .en(miss), .clk(in_3), .Q(stall), .clr(or_1_out));
  or or_1 (or_1_out, novoBlocoPronto, reset);
  Comparator #(.mode("unsigned"), .width(3)) comparator_1 (.a(adder_1_out), .b(3'b101), .gt(fimWb));  // open: eq, lt
  not not_1 (not_1_out, fimWb);
  Multiplexer #(.select(2), .width(4)) multiplexer_2 (
    .in0(tagR0), .in1(tagR1), .in2(tagR2), .in3(tagR3), .out(multiplexer_2_out), .sel(address[3:2]));
  Register #(.width(3)) register_2 (.D(adder_1_out), .en(memWrite), .clk(clkMem), .Q(register_2_q), .clr(not_2_out));
  and and_1 (memWrite, not_1_out, stall);
  not not_2 (not_2_out, stall);
  Adder #(.width(3)) adder_1 (.a(3'b001), .b(register_2_q), .out(adder_1_out));  // open: cin, cout
  Subtractor #(.width(2)) subtractor_1 (.a(register_2_q[1:0]), .b(2'b01), .out(subtractor_1_out));  // open: bin, bout
  Comparator #(.mode("unsigned"), .width(3)) comparator_2 (
    .a(adder_2_out), .b(3'b100), .gt(novoBlocoPronto));  // open: eq, lt
  not not_3 (not_3_out, novoBlocoPronto);
  and and_2 (and_2_out, not_3_out, fimWb, stall);
  Register #(.width(3)) register_3 (
    .D(adder_2_out), .en(and_2_out), .clk(clkMem), .Q({register_3_q_2[2], register_3_q}), .clr(not_4_out));
  not not_4 (not_4_out, stall);
  Multiplexer #(.width(8)) multiplexer_3 (
    .in0({multiplexer_2_out, multiplexer_1_out, subtractor_1_out}),
    .in1({address[7:4], multiplexer_1_out, register_3_q}), .out(memAddress), .sel(fimWb));
  Adder #(.width(3)) adder_2 (.a(3'b001), .b({register_3_q_2[2], register_3_q}), .out(adder_2_out));  // open: cin, cout

  assign memRead = fimWb;
  assign memValue = cacheIn;

  // Other names for the same wires on the sheet: tagNova[3:0] = address[7:4]

  // Notes on the sheet:
  //   tag-nova
  //   index
  //   fim do wb
  //   começa em tag 00 até tag 11
  //   tag
  //   offset
  //   puxou novo bloco
endmodule

module PC (
  input  Jump,
  input  [7:0] NewPC,
  input  Stall,
  input  Clock,
  input  Reset,
  output LimpaPipe,
  output [7:0] SaidaPC,
  output [7:0] SaidaPC2,
  output ClockDiv2
);

  wire clk, d_ff_1_q, d_ff_2_q, d_ff_3_qn, multiplexer_1_out, not_1_out;
  wire [7:0] multiplexer_2_out;

  or or_1 (LimpaPipe, Reset, d_ff_2_q);
  Multiplexer multiplexer_1 (.in0(1'b1), .in1(1'b0), .out(multiplexer_1_out), .sel(d_ff_2_q));
  and and_1 (clk, not_1_out, Clock);
  not not_1 (not_1_out, Stall);
  D_Flip_Flop d_ff_1 (.D(d_ff_3_qn), .clk(Clock), .Q(d_ff_1_q), .reset(Reset));  // open: Qn, preset
  D_Flip_Flop d_ff_2 (.D(Jump), .clk(clk), .Q(d_ff_2_q), .reset(Reset));  // open: Qn, preset
  Register register_1 (.D(multiplexer_2_out), .en(multiplexer_1_out), .clk(clk), .Q(SaidaPC2), .clr(Reset));
  Multiplexer #(.width(8)) multiplexer_2 (.in0(SaidaPC), .in1(NewPC), .out(multiplexer_2_out), .sel(Jump));
  D_Flip_Flop d_ff_3 (.D(d_ff_1_q), .clk(Clock), .Q(ClockDiv2), .Qn(d_ff_3_qn), .reset(Reset));  // open: preset
  Adder adder_1 (.a(8'h1), .b(SaidaPC2), .out(SaidaPC));  // open: cin, cout
endmodule

module Contador (
  input  [7:0] botao,
  input  Clock,
  output [3:0] ZeroAtres,
  output [3:0] QuatroASete,
  output [3:0] OitoAOnze,
  output [3:0] DozeAQuinze
);

  wire comparator_1_eq, comparator_2_lt, d_ff_1_q, d_ff_2_q, not_1_out;
  wire [15:0] bit_extender_1_out, counter_1_q, register_1_q, register_2_q;

  Comparator comparator_1 (.a(botao), .b({8{1'b0}}), .eq(comparator_1_eq));  // open: gt, lt
  D_Flip_Flop d_ff_1 (.D(comparator_1_eq), .clk(Clock), .Q(d_ff_1_q));  // open: Qn, preset, reset
  not not_1 (not_1_out, d_ff_1_q);
  D_Flip_Flop d_ff_2 (.D(d_ff_1_q), .clk(Clock), .Q(d_ff_2_q));  // open: Qn, preset, reset
  Counter #(.max('hffff), .width(16)) counter_1 (.Q(counter_1_q), .clk(Clock));  // open: load, D, count, carry, up, clr
  Register #(.width(16)) register_1 (.D(counter_1_q), .en(not_1_out), .clk(Clock), .Q(register_1_q));  // open: clr
  Register #(.width(16)) register_2 (.D(register_1_q), .en(not_1_out), .clk(Clock), .Q(register_2_q));  // open: clr
  Comparator #(.width(16)) comparator_2 (.a(16'h1), .b(register_2_q), .lt(comparator_2_lt));  // open: gt, eq
  assign bit_extender_1_out = {{15{1'b0}}, comparator_2_lt};  // Bit_Extender bit_extender_1
  Adder #(.width(16)) adder_1 (
    .a(bit_extender_1_out), .b(register_2_q), .out({DozeAQuinze, OitoAOnze, QuatroASete, ZeroAtres}),
    .cin(d_ff_2_q));  // open: cout
endmodule
